// Logisim project adder-master.circ as structural Verilog: 1 circuit, main circuit main
module main (
  input  [1:0] a,
  input  [1:0] b,
  output [2:0] sum
);

  Adder #(.width(2)) adder_1 (.a(a), .b(b), .out(sum[1:0]), .cout(sum[2]));  // open: cin
endmodule
