// Logisim project adder-query.circ as structural Verilog: 3 circuits, main circuit main
module main (
  input  [1:0] a,
  input  [1:0] b,
  output [2:0] out_3
);

  halfadder HA (.a0(a[0]), .b0(b[0]), .SUM(out_3[0]));  // open: carry
  fulladder FA (.A(b[1]), .B(a[1]), .C_prime(out_3[2]), .s(out_3[1]));  // open: C
endmodule

module halfadder (
  input  a0,
  input  b0,
  output SUM,
  output carry
);

  xor xor_1 (SUM, a0, b0);
  and and_1 (carry, a0, b0);
endmodule

module fulladder (
  input  C,
  input  A,
  input  B,
  output s,
  output C_prime
);

  wire and_1_out, and_2_out, xor_1_out;

  xor xor_1 (xor_1_out, A, B);
  and and_1 (and_1_out, C, xor_1_out);
  and and_2 (and_2_out, B, A);
  or or_1 (C_prime, and_2_out, and_1_out);
  xor xor_2 (s, xor_1_out, C);
endmodule
