// Logisim project adder-test.circ as structural Verilog: 2 circuits, main circuit main
module main (
  output [1:0] A,
  output [1:0] B,
  output [2:0] Y,
  output halt
);

  wire clock_1_out;

  Clock clock_1 (.out(clock_1_out));
  Counter #(.width(4), .max('hf)) counter_1 (.Q({B, A}), .carry(halt), .clk(clock_1_out));  // open: load, D, count, clr
  adder_master_main main_1 (.a(A), .b(B), .sum(Y));
endmodule

module _2_bit (
  input  [1:0] A,
  input  [1:0] B,
  output [2:0] Y
);

  Adder #(.width(2)) adder_1 (.a(A), .b(B), .out(Y[1:0]), .cout(Y[2]));  // open: cin
endmodule
