// Logisim project main-tester.circ as structural Verilog: 1 circuit, main circuit main
module main (
  output halt,
  output [1:0] out_2,
  output [1:0] out_3,
  output [1:0] out_4,
  output [1:0] out_5
);

  wire clock_1_out;

  Counter #(.width(6), .max('h3f)) counter_1 (
    .Q({out_2, out_3, out_4}), .carry(halt), .clk(clock_1_out));  // open: load, D, count, clr
  Clock clock_1 (.out(clock_1_out));
  correct_circuit_main main_1 (.A(out_4), .B(out_3), .C(out_2), .out_4(out_5));

  // Other names for the same wires on the sheet: inputA[1:0] = out_4; inputB[1:0] = out_3; inputC[1:0] = out_2;
  //   output[1:0] = out_5

  // Notes on the sheet:
  //   A splitter splits the counter value into input values.
  //   the library loaded circuit
  //   The number of bits for the counter should be the sum of the number of input bits.
  //   For example, if there are 3 inputs with 2 bits each, the number of bits should be 6.
  //   this will be used to generate the correct output and for substituting student work
  //   output display: topleft output is the left most column in the table
endmodule
