// Logisim project LogicGate.circ as structural Verilog: 1 circuit, main circuit main
module main (
  input  [1:0] A,
  input  [1:0] B,
  input  [1:0] C,
  output [1:0] out_4
);

  wire [1:0] and_1_out, and_2_out;

  assign and_1_out = A & ~B & C;  // AND_Gate and_1, 2 bits wide
  assign and_2_out = ~A & B & C;  // AND_Gate and_2, 2 bits wide
  assign out_4 = and_1_out | and_2_out;  // OR_Gate or_1, 2 bits wide

  // Notes on the sheet:
  //   incorrect circuit
  //   wrong circuit design
endmodule
