// Logisim project LogicGate.circ as structural Verilog: 1 circuit, main circuit main
module main (
  input  [1:0] B,
  input  [1:0] C,
  input  [1:0] A,
  output [1:0] out
);

  wire [1:0] and_1_out, and_2_out;

  assign and_1_out = B & ~C & A;  // AND_Gate and_1, 2 bits wide
  assign and_2_out = C & B & ~A;  // AND_Gate and_2, 2 bits wide
  assign out = and_1_out | and_2_out;  // OR_Gate or_1, 2 bits wide

  // Notes on the sheet:
  //   incorrect circuit
  //   technically right, but input order not respected (not A,B,C)
endmodule
