// Logisim project LogicGate.circ as structural Verilog: 1 circuit, main circuit main
module main (
  input  A0,
  input  A1,
  input  B0,
  input  B1,
  input  C0,
  input  C1,
  output Y0,
  output Y1
);

  wire and_1_out, and_2_out, and_3_out, and_4_out;

  and and_1 (and_1_out, A0, B0, ~C0);  // AND_Gate
  and and_2 (and_2_out, ~A0, B0, C0);  // AND_Gate
  and and_3 (and_3_out, A1, B1, ~C1);  // AND_Gate
  and and_4 (and_4_out, ~A1, B1, C1);  // AND_Gate
  or or_1 (Y0, and_1_out, and_2_out);
  or or_2 (Y1, and_3_out, and_4_out);

  // Notes on the sheet:
  //   incorrect circuit
  //   wrong number and data size for inputs and outputs
endmodule
