// Logisim project LogicGate.circ as structural Verilog: 1 circuit, main circuit main
module main (
  input  [1:0] A,
  input  [1:0] B,
  input  [1:0] C,
  output [1:0] \output 
);

  wire [1:0] and_1_out, and_2_out;

  assign and_1_out = A & B & ~C;  // AND_Gate and_1, 2 bits wide
  assign \output  = and_1_out | and_2_out;  // OR_Gate or_1, 2 bits wide
  assign and_2_out = ~A & B & C;  // AND_Gate and_2, 2 bits wide

  // Notes on the sheet:
  //   incorrect circuit
  //   Wrong orientation of input and output
endmodule
