// Logisim project LogicGate.circ as structural Verilog: 2 circuits, main circuit main
module main (
  input  [1:0] B,
  input  [1:0] A,
  input  [1:0] C,
  output [1:0] \output 
);

  wire [1:0] and_1_out, and_2_out;

  assign and_1_out = A & B & ~C;  // AND_Gate and_1, 2 bits wide
  assign \output  = and_1_out | and_2_out;  // OR_Gate or_1, 2 bits wide
  assign and_2_out = ~A & B & C;  // AND_Gate and_2, 2 bits wide

  // Notes on the sheet:
  //   correct circuit
  //   Would be incorrect since the normal input order would be BAC
  //   but the input order was corrected in the appearance
endmodule

module dd (
  input  [1:0] B,
  input  [1:0] A,
  input  [1:0] C,
  output [1:0] \output 
);

  wire [1:0] and_1_out, and_2_out;

  assign and_1_out = A & B & ~C;  // AND_Gate and_1, 2 bits wide
  assign \output  = and_1_out | and_2_out;  // OR_Gate or_1, 2 bits wide
  assign and_2_out = ~A & B & C;  // AND_Gate and_2, 2 bits wide
endmodule
