// Logisim project LogicGate.circ as structural Verilog: 1 circuit, main circuit main
module main (
  input  [1:0] A,
  input  [1:0] B,
  input  [1:0] C,
  output [1:0] out_4
);

  wire [1:0] and_1_out, and_2_out, not_1_out, not_2_out;

  assign not_1_out = ~C;  // NOT_Gate not_1, 2 bits wide
  assign not_2_out = ~A;  // NOT_Gate not_2, 2 bits wide
  assign and_1_out = A & B & not_1_out;  // AND_Gate and_1, 2 bits wide
  assign and_2_out = not_2_out & B & C;  // AND_Gate and_2, 2 bits wide
  assign out_4 = and_1_out | and_2_out;  // OR_Gate or_1, 2 bits wide

  // Notes on the sheet:
  //   incorrect circuit
  //   Same circuit as student A but the order of inputs changed in circuit appearance
endmodule
