// Logisim project main-checker.circ as structural Verilog: 1 circuit, main circuit main
module main (
  output [7:0] out,
  output halt,
  output isZero
);

  RAM_main main_1 (.out_1(out), .halt(halt));
  Hex_Digit_Display hex_digit_display_1 (.value(out[7:4]));  // open: dp
  Hex_Digit_Display hex_digit_display_2 (.value(out[3:0]));  // open: dp
  Comparator comparator_1 (.a(out), .b({8{1'b0}}), .eq(isZero));  // open: gt, lt

  // Notes on the sheet:
  //   does not show up in command line
endmodule
