// Logisim project rom-example.circ as structural Verilog: 1 circuit, main circuit main
module main (
  output [7:0] out,
  output halt
);

  wire clock_1_out;
  wire [7:0] counter_1_q;

  Counter counter_1 (.Q(counter_1_q), .clk(clock_1_out));  // open: load, D, count, carry, clr
  Clock clock_1 (.out(clock_1_out));
  Comparator comparator_1 (.a(counter_1_q), .b(8'h5), .eq(halt));  // open: gt, lt
  ROM rom_1 (.addr(counter_1_q), .data(out));  // open: sel
endmodule
