// Logisim project random-circuit.circ as structural Verilog: 2 circuits, main circuit main
module main (
  input  [3:0] A,
  input  [3:0] B,
  output [3:0] Y
);

  assign Y = A ^ B;  // XOR_Gate xor_1, 4 bits wide
endmodule

module exp (
  input  A,
  input  B,
  input  C,
  input  AA0,
  input  AA1,
  input  AA2,
  input  [2:0] BB,
  output X,
  output [2:0] Y
);

  and and_1 (X, A, B, C);
  assign Y = {AA2, AA1, AA0} | BB;  // OR_Gate or_1, 3 bits wide
endmodule
